# Fritzing sketch shieldPCB (saved by Fritzing 0.9.3b)

parts:
  Part1 = Arduino Due (Rev2b)
  M1 = RioRand LM2596
  Part2 = Motor Driver 1A Dual TB6612FNG
  U1 = LM124-324 Quad Opamp [package="DIP (Dual Inline)"]
  U2 = LM124-324 Quad Opamp [package="DIP (Dual Inline)"]
  U3 = LM124-324 Quad Opamp [package="DIP (Dual Inline)"]
  J1 = Dagu DGServo 9g header (male) [package=THT]
  J3 = Dagu DGServo 9g header (male) [package=THT]
  J4 = Dagu DGServo 9g header (male) [package=THT]
  U4 = POT [package=pot_alpha_rv16af-20]
  J5 = Dagu DGServo 9g header (male) [package=THT]
  S1 = Toggle Switch [package=THT]
  J6 = single row smd male pin header, 4 pins [form="♂ (male)"]

nets:
  N1: Part1.DAC0, S1.L1
  N2: Part1.IOREF, U1.VCC+, U2.VCC+, U3.VCC+, U4.A
  N3: Part1.GND, U1.VCC-, U2.VCC-, U3.VCC-, U4.E
  N4: Part1.D8_PWM, Part2.STBY
  N5: Part1.D2_PWM, Part2.PWMA
  N6: Part1.D3_PWM, Part2.AIN2
  N7: Part1.D4_PWM/SS1, Part2.AIN1
  N8: Part1.D5_PWM, Part2.BIN1
  N9: Part1.D6_PWM, Part2.BIN2
  N10: Part1.D7_PWM, Part2.PWMB
  N11: Part1.D30, U3.4OUT
  N12: Part1.D32, U3.3OUT
  N13: Part1.D34, U3.2OUT
  N14: Part1.D36, U3.1OUT
  N15: Part1.D38, U1.4OUT
  N16: Part1.D40, U1.3OUT
  N17: Part1.D42, U1.2OUT
  N18: Part1.D44, U1.1OUT
  N19: Part1.D46, U2.4OUT
  N20: Part1.D48, U2.1OUT
  N21: Part1.D50, U2.2OUT
  N22: Part1.D52, U2.3OUT
  N23: M1.Pin_3, Part2.VM
  N24: M1.Pin_4, Part2.GND
  N25: Part2.B01, J6.pin1
  N26: Part2.B02, J6.pin2
  N27: Part2.A02, J6.pin3
  N28: Part2.A01, J6.pin4
  N29: U1.1IN-, U1.2IN-, U1.3IN-, U1.4IN-, U2.1IN-, U2.2IN-, U2.3IN-, U2.4IN-, U3.1IN-, U3.2IN-, U3.3IN-, U3.4IN-, S1.COM
  N30: U1.1IN+, J3.gnd
  N31: U1.2IN+, J3.Vcc
  N32: U1.3IN+, J5.pulse
  N33: U1.4IN+, J5.Vcc
  N34: U2.1IN+, J4.pulse
  N35: U2.2IN+, J4.Vcc
  N36: U2.3IN+, J3.pulse
  N37: U2.4IN+, J4.gnd
  N38: U3.1IN+, J5.gnd
  N39: U3.2IN+, J1.pulse
  N40: U3.3IN+, J1.Vcc
  N41: U3.4IN+, J1.gnd
  N42: U4.S, S1.L2
