# Fritzing sketch sensors (saved by Fritzing 0.9.3b)
circuit board: 10.7cm x 5.64cm
breadboards: 1

parts:
  R4 = LED - 3mm [color="Red (633nm)" package="3 mm [THT]"]
  T4 = LED - 3mm [color="Red (633nm)" package="3 mm [THT]"]
  T3 = LED - 3mm [color="Red (633nm)" package="3 mm [THT]"]
  R3 = LED - 3mm [color="Red (633nm)" package="3 mm [THT]"]
  R5 = LED - 3mm [color="Red (633nm)" package="3 mm [THT]"]
  T5 = LED - 3mm [color="Red (633nm)" package="3 mm [THT]"]
  R6 = LED - 3mm [color="Red (633nm)" package="3 mm [THT]"]
  T6 = LED - 3mm [color="Red (633nm)" package="3 mm [THT]"]
  T2 = LED - 3mm [color="Red (633nm)" package="3 mm [THT]"]
  R2 = LED - 3mm [color="Red (633nm)" package="3 mm [THT]"]
  T1 = LED - 3mm [color="Red (633nm)" package="3 mm [THT]"]
  R1 = LED - 3mm [color="Red (633nm)" package="3 mm [THT]"]
  T0 = LED - 3mm [color="Red (633nm)" package="3 mm [THT]"]
  R0 = LED - 3mm [color="Red (633nm)" package="3 mm [THT]"]
  R7 = LED - 3mm [color="Red (633nm)" package="3 mm [THT]"]
  T7 = LED - 3mm [color="Red (633nm)" package="3 mm [THT]"]
  R8 = LED - 3mm [color="Red (633nm)" package="3 mm [THT]"]
  T8 = LED - 3mm [color="Red (633nm)" package="3 mm [THT]"]
  GND = female pin header, 1 pin [form="♀ (female)"]
  3_3v = female pin header, 1 pin [form="♀ (female)"]
  5v = female pin header, 1 pin [form="♀ (female)"]
  Q0 = TRANSISTOR_NPN [package=to-92]
  10k = Resistor [tolerance=±5% resistance=220 package=THT]
  10k_2 = Resistor [tolerance=±5% resistance=220 package=THT]
  10k_3 = Resistor [tolerance=±5% resistance=220 package=THT]
  Q1 = TRANSISTOR_NPN [package=to-92]
  Q2 = TRANSISTOR_NPN [package=to-92]
  100 = Resistor [tolerance=±5% resistance=220 package=THT]
  R0-3 = female pin header, 4 pins [form="♀ (female)"]
  10k_4 = Resistor [tolerance=±5% resistance=220 package=THT]
  10k_5 = Resistor [tolerance=±5% resistance=220 package=THT]
  10k_6 = Resistor [tolerance=±5% resistance=220 package=THT]
  10k_7 = Resistor [tolerance=±5% resistance=220 package=THT]
  C0-2 = female pin header, 3 pins [form="♀ (female)"]
  R5-8 = female pin header, 4 pins [form="♀ (female)"]
  10k_8 = Resistor [tolerance=±5% resistance=220 package=THT]
  10k_9 = Resistor [tolerance=±5% resistance=220 package=THT]
  10k_10 = Resistor [tolerance=±5% resistance=220 package=THT]
  10k_11 = Resistor [tolerance=±5% resistance=220 package=THT]
  GND_2 = female pin header, 1 pin [form="♀ (female)"]
  GND_3 = female pin header, 1 pin [form="♀ (female)"]
  R4_2 = female pin header, 1 pin [form="♀ (female)"]
  10k_12 = Resistor [tolerance=±5% resistance=220 package=THT]

nets:
  N1: R4.cathode, R3.cathode, R5.cathode, R6.cathode, R2.cathode, R1.cathode, R0.cathode, R7.cathode, R8.cathode, 3_3v.pin1
  N2: R4.anode, R4_2.pin1, 10k_12.Pin_0
  N3: T4.cathode, T3.anode, T5.anode, T6.anode, T2.anode, T1.anode, T0.anode, T7.anode, T8.anode, 100.Pin_1
  N4: T4.anode, Q1.C
  N5: T3.cathode, T2.cathode, T1.cathode, T0.cathode, Q0.C
  N6: R3.anode, R0-3.pin4, 10k_7.Pin_0
  N7: R5.anode, R5-8.pin1, 10k_11.Pin_0
  N8: T5.cathode, T6.cathode, T7.cathode, T8.cathode, Q2.C
  N9: R6.anode, R5-8.pin2, 10k_9.Pin_0
  N10: R2.anode, R0-3.pin3, 10k_5.Pin_0
  N11: R7.anode, R5-8.pin3, 10k_10.Pin_0
  N12: GND.pin1, Q0.E, Q1.E, Q2.E, 10k_4.Pin_1, 10k_5.Pin_1, 10k_6.Pin_1, 10k_7.Pin_1
  N13: 5v.pin1, 100.Pin_0
  N14: Q0.B, 10k.Pin_0
  N15: 10k.Pin_1, C0-2.pin1
  N16: 10k_2.Pin_0, Q1.B
  N17: 10k_2.Pin_1, C0-2.pin2
  N18: 10k_3.Pin_0, Q2.B
  N19: 10k_3.Pin_1, C0-2.pin3
  N20: R0-3.pin1, 10k_6.Pin_0
  N21: R0-3.pin2, 10k_4.Pin_0
  N22: R5-8.pin4, 10k_8.Pin_0
  N23: 10k_8.Pin_1, 10k_9.Pin_1, 10k_10.Pin_1, 10k_11.Pin_1, GND_2.pin1
  N24: GND_3.pin1, 10k_12.Pin_1
