# Fritzing sketch ShieldPCB (saved by Fritzing 0.9.3b)
circuit board: 14.531cm x 9.95714cm
breadboards: 1

parts:
  J8 = male pin header, 4 pins [form="♂ (male)"]
  S4 = Momentary Switch [package=ksa_sealed_tac_switch]
  S5 = Momentary Switch [package=ksa_sealed_tac_switch]
  LED3 = LED - 3mm [color="Yellow (574nm)" package="3 mm [THT]"]
  LED4 = LED - 3mm [color="Red (633nm)" package="3 mm [THT]"]
  J9 = female pin header, 6 pins [form="♀ (female)"]
  Part4 = Motor Driver 1A Dual TB6612FNG
  S6 = Toggle Switch [package=THT]
  R1 = TRIMPOT [package=trim_pot_pth]
  R2 = Resistor [tolerance=±5% resistance=330 package=THT]
  Part3 = Arduino Due (Rev2b)
  J15 = female pin header, 15 pins [form="♀ (female)"]
  J14 = male pin header, 18 pins [form="♂ (male)"]
  U7 = LM124-324 Quad Opamp [package="DIP (Dual Inline)"]
  U8 = LM124-324 Quad Opamp [package="DIP (Dual Inline)"]
  U9 = LM124-324 Quad Opamp [package="DIP (Dual Inline)"]

nets:
  N1: J8.pin1, Part4.A01
  N2: J8.pin2, Part4.A02
  N3: J8.pin3, Part4.B02
  N4: J8.pin4, Part4.B01
  N5: S4.1, R2.Pin_0, U8.VCC-
  GND: S4.2, S5.4, J9.pin3, Part4.GND, R1.CCW, Part3.GND, J15.pin3, J14.pin1, U9.VCC-
  N6: S4.4, Part3.D42
  N7: S5.2, Part3.D48
  N8: LED3.cathode, LED4.cathode, R2.Pin_1
  N9: LED3.anode, Part3.D36
  N10: LED4.anode, Part3.D40
  N11: J9.pin2, Part3.5V, J15.pin2, J14.pin18
  N12: J9.pin4, Part3.D18/TX1
  N13: J9.pin5, Part3.D19/RX1
  N14: Part4.VCC, R1.CW, Part3.IOREF, J15.pin1, U7.VCC+, U7.VCC-, U8.VCC+, U9.VCC+
  N15: Part4.PWMA, Part3.D13_PWM
  N16: Part4.AIN2, Part3.D12_PWM
  N17: Part4.AIN1, Part3.D5_PWM
  N18: Part4.BIN1, Part3.D4_PWM/SS1
  N19: Part4.BIN2, Part3.D3_PWM
  N20: Part4.PWMB, Part3.D2_PWM
  N21: S6.L1, Part3.DAC0
  N22: S6.COM, U7.1IN-, U7.2IN-, U7.3IN-, U7.4IN-, U8.1IN-, U8.2IN-, U8.3IN-, U8.4IN-, U9.1IN-, U9.2IN-, U9.3IN-, U9.4IN-
  N23: S6.L2, R1.WIPER
  N24: Part3.A8, J15.pin12, U8.4IN+
  N25: Part3.A9, J15.pin13
  N26: Part3.A10, J15.pin14
  N27: Part3.A11, J15.pin15
  N28: Part3.A0, J15.pin4, U7.1IN+
  N29: Part3.A1, J15.pin5, U7.4IN+
  N30: Part3.A2, J15.pin6, U7.3IN+
  N31: Part3.A3, J15.pin7, U9.4IN+
  N32: Part3.A4, J15.pin8, U9.3IN+
  N33: Part3.A5, J15.pin9, U7.2IN+
  N34: Part3.A6, J15.pin10, U8.1IN+
  N35: Part3.A7, J15.pin11, U8.3IN+
  N36: Part3.D8_PWM, U9.4OUT
  N37: Part3.D9_PWM, U7.1OUT
  N38: Part3.D10_PWM/SS0, U7.3OUT
  N39: Part3.D11_PWM, U7.4OUT
  N40: Part3.D22, U9.3OUT
  N41: Part3.D23, J14.pin17
  N42: Part3.D24, U9.2OUT
  N43: Part3.D25, J14.pin16
  N44: Part3.D26, U9.1OUT
  N45: Part3.D27, J14.pin15
  N46: Part3.D28, U7.2OUT
  N47: Part3.D29, J14.pin14
  N48: Part3.D31, J14.pin13
  N49: Part3.D32, U8.1OUT
  N50: Part3.D33, J14.pin12
  N51: Part3.D35, J14.pin11
  N52: Part3.D37, J14.pin10
  N53: Part3.D39, J14.pin9
  N54: Part3.D41, J14.pin8
  N55: Part3.D43, J14.pin7
  N56: Part3.D44, U8.4OUT
  N57: Part3.D45, J14.pin6
  N58: Part3.D47, J14.pin5
  N59: Part3.D49, J14.pin4
  N60: Part3.D50, U8.3OUT
  N61: Part3.D51, J14.pin3
  N62: Part3.D53, J14.pin2
