# Fritzing sketch shieldPCB (saved by Fritzing 0.9.3b)
circuit board: 9.80044cm x 7.59288cm

parts:
  Part1 = Arduino Due (Rev2b)
  Part2 = Motor Driver 1A Dual TB6612FNG
  U1 = LM124-324 Quad Opamp [package="DIP (Dual Inline)"]
  U2 = LM124-324 Quad Opamp [package="DIP (Dual Inline)"]
  U3 = LM124-324 Quad Opamp [package="DIP (Dual Inline)"]
  S1 = Toggle Switch [package=THT]
  JP2 = Header 2 [package=screwterminal-3.5mm-2_lock]
  R2 = TRIMPOT [package=trim_pot_pth]
  J17 = female pin header, 6 pins [form="♀ (female)"]
  J6 = male pin header, 4 pins [form="♂ (male)"]
  S5 = Momentary Switch [package=ksa_sealed_tac_switch]
  S6 = Momentary Switch [package=ksa_sealed_tac_switch]
  LED4 = LED - 3mm [color="Yellow (574nm)" package="3 mm [THT]"]
  LED5 = LED - 3mm [color="Yellow (574nm)" package="3 mm [THT]"]
  R3 = Resistor [tolerance=±5% resistance=330 package=THT]
  J18 = male pin header, 18 pins [form="♂ (male)"]
  C1 = Ceramic Capacitor [capacitance=100nF package="100 mil [THT, multilayer]"]
  C3 = Ceramic Capacitor [capacitance=100nF package="100 mil [THT, multilayer]"]
  J19 = female pin header, 4 pins [form="♀ (female)"]
  J16 = male pin header, 16 pins [form="♂ (male)"]

nets:
  N1: Part1.A8, U3.1IN+, J16.pin5
  N2: Part1.A9, U3.2IN+, J16.pin4
  N3: Part1.A10, U3.4IN+, J16.pin3
  N4: Part1.A11, U3.3IN+, J16.pin2
  N5: Part1.DAC0, S1.L1
  N6: Part1.DAC1, J16.pin1
  N7: Part1.A0, U2.3IN+, J16.pin13
  N8: Part1.A1, U2.4IN+, J16.pin12
  N9: Part1.A2, U2.1IN+, J16.pin11
  N10: Part1.A3, U2.2IN+, J16.pin10
  N11: Part1.A4, U1.4IN+, J16.pin9
  N12: Part1.A5, U1.1IN+, J16.pin8
  N13: Part1.A6, U1.2IN+, J16.pin7
  N14: Part1.A7, U1.3IN+, J16.pin6
  N15: Part1.D14/TX3, LED5.anode
  N16: Part1.D15/RX3, LED4.anode
  N17: Part1.D18/TX1, J17.pin4
  N18: Part1.D19/RX1, J17.pin5
  N19: Part1.IOREF, U1.VCC+, U2.VCC+, U3.VCC+, R2.CCW, J16.pin16
  N20: Part1.5V, J17.pin2, J18.pin18, J19.pin1, J16.pin15
  GND: Part1.GND, Part2.GND, U1.VCC-, U2.VCC-, U3.VCC-, JP2.1, R2.CW, J17.pin3, S5.3, S6.1, S6.2, R3.Pin_1, J18.pin1, C3.0, J19.pin4, J16.pin14
  N21: Part1.VIN, Part2.VM, JP2.2
  N22: Part1.D8_PWM, Part2.BIN2
  N23: Part1.D9_PWM, Part2.BIN1
  N24: Part1.D10_PWM/SS0, Part2.AIN1
  N25: Part1.D11_PWM, Part2.AIN2
  N26: Part1.D12_PWM, Part2.PWMA
  N27: Part1.D13_PWM, Part2.STBY
  N28: Part1.D2_PWM, S6.4, C3.1
  N29: Part1.D3_PWM, U2.2OUT
  N30: Part1.D4_PWM/SS1, U2.1OUT
  N31: Part1.D5_PWM, U2.4OUT
  N32: Part1.D6_PWM, U2.3OUT
  N33: Part1.D7_PWM, Part2.PWMB
  N34: Part1.D22, J19.pin3
  N35: Part1.D23, J18.pin17
  N36: Part1.D24, J19.pin2
  N37: Part1.D25, J18.pin16
  N38: Part1.D26, U1.3OUT
  N39: Part1.D27, J18.pin15
  N40: Part1.D28, U1.1OUT
  N41: Part1.D29, J18.pin14
  N42: Part1.D30, U1.2OUT
  N43: Part1.D31, J18.pin13
  N44: Part1.D32, U3.1OUT
  N45: Part1.D33, J18.pin12
  N46: Part1.D34, U3.4OUT
  N47: Part1.D35, J18.pin11
  N48: Part1.D36, U3.3OUT
  N49: Part1.D37, J18.pin10
  N50: Part1.D38, U3.2OUT
  N51: Part1.D39, J18.pin9
  N52: Part1.D40, U1.4OUT
  N53: Part1.D41, J18.pin8
  N54: Part1.D43, J18.pin7
  N55: Part1.D45, J18.pin6
  N56: Part1.D47, J18.pin5
  N57: Part1.D49, J18.pin4
  N58: Part1.D50, S5.2, C1.0
  N59: Part1.D51, J18.pin3
  N60: Part1.D53, J18.pin2
  N61: Part2.B01, J6.pin1
  N62: Part2.B02, J6.pin2
  N63: Part2.A02, J6.pin3
  N64: Part2.A01, J6.pin4
  N65: U1.1IN-, U1.2IN-, U1.3IN-, U1.4IN-, U2.1IN-, U2.2IN-, U2.3IN-, U2.4IN-, U3.1IN-, U3.2IN-, U3.3IN-, U3.4IN-, S1.COM
  N66: S1.L2, R2.WIPER
  N67: S5.4, C1.1
  N68: LED4.cathode, LED5.cathode, R3.Pin_0

notes:
  5v
  Gnd
  Vcc
  330
  3.3v
  Tx
  Rx
  |-----------IR Sensors------------|
  Sensors
  DAC1
